// Logisim project 03b_adder_subtractor_solution.circ as structural Verilog: 4 circuits, main circuit HA
module HA (
  input  A,
  input  B,
  output S,
  output C
);

  xor xor_1 (S, A, B);
  and and_1 (C, A, B);
endmodule

module FA (
  input  Cin,
  input  A,
  input  B,
  output S,
  output Cout
);

  wire ha_1_c, ha_1_s, ha_2_c;

  HA ha_1 (.A(A), .B(B), .S(ha_1_s), .C(ha_1_c));
  HA ha_2 (.A(Cin), .B(ha_1_s), .S(S), .C(ha_2_c));
  or or_1 (Cout, ha_2_c, ha_1_c);
endmodule

module RCAdder (
  input  A0,
  input  A1,
  input  A2,
  input  A3,
  input  B0,
  input  B1,
  input  B2,
  input  B3,
  output S0,
  output S1,
  output S2,
  output S3,
  output Cout
);

  wire fa_1_cout, fa_2_cout, ha_1_c;

  HA ha_1 (.A(A0), .B(B0), .S(S0), .C(ha_1_c));
  FA fa_1 (.Cin(ha_1_c), .A(A1), .B(B1), .S(S1), .Cout(fa_1_cout));
  FA fa_2 (.Cin(fa_1_cout), .A(A2), .B(B2), .S(S2), .Cout(fa_2_cout));
  FA fa_3 (.Cin(fa_2_cout), .A(A3), .B(B3), .S(S3), .Cout(Cout));
endmodule

module AdderSubtractor (
  input  M,
  input  A0,
  input  A1,
  input  A2,
  input  A3,
  input  B0,
  input  B1,
  input  B2,
  input  B3,
  output S0,
  output S1,
  output S2,
  output S3,
  output Cout
);

  wire fa_1_cout, fa_2_cout, fa_3_cout, xor_1_out, xor_2_out, xor_3_out, xor_4_out;

  xor xor_1 (xor_1_out, M, B0);
  xor xor_2 (xor_2_out, M, B1);
  xor xor_3 (xor_3_out, M, B2);
  xor xor_4 (xor_4_out, M, B3);
  FA fa_1 (.Cin(M), .A(A0), .B(xor_1_out), .S(S0), .Cout(fa_1_cout));
  FA fa_2 (.Cin(fa_1_cout), .A(A1), .B(xor_2_out), .S(S1), .Cout(fa_2_cout));
  FA fa_3 (.Cin(fa_2_cout), .A(A2), .B(xor_3_out), .S(S2), .Cout(fa_3_cout));
  FA fa_4 (.Cin(fa_3_cout), .A(A3), .B(xor_4_out), .S(S3), .Cout(Cout));
endmodule
