// Logisim project basic_gates_and_half_adder.circ as structural Verilog: 1 circuit, main circuit main
module main (
  input  in_1,
  input  in_2,
  input  in_3,
  input  in_4,
  input  in_5,
  input  A,
  input  B,
  input  AA,
  input  BB,
  input  in_10,
  input  in_11,
  input  in_12,
  input  in_13,
  input  in_14,
  input  in_15,
  input  X,
  input  Y,
  output NOT1,
  output AND4,
  output AND2,
  output OR2,
  output XOR2,
  output NAND2,
  output NOR2,
  output S,
  output C
);

  and and_1 (C, X, Y);
  not not_1 (NOT1, in_1);
  and and_2 (AND4, in_2, in_3, in_4, in_5);
  and and_3 (AND2, A, B);
  or or_1 (OR2, AA, BB);
  xor xor_1 (XOR2, in_10, in_11);
  nand nand_1 (NAND2, in_12, in_13);
  nor nor_1 (NOR2, in_14, in_15);
  xor xor_2 (S, X, Y);

  // Notes on the sheet:
  //   Half Adder
  //   4-input AND
endmodule
