// Logisim project canonical_sop_incomplete.circ as structural Verilog: 1 circuit, main circuit main
module main (
  input  A0,
  input  A1,
  input  A2,
  output out_4
);

  wire and_1_out, and_2_out, and_3_out, and_4_out, not_1_out, not_2_out, not_3_out;

  not not_1 (not_1_out, A0);
  not not_2 (not_2_out, A1);
  not not_3 (not_3_out, A2);
  and and_1 (and_1_out, A2, not_2_out, not_1_out);
  and and_2 (and_2_out, A2, not_2_out, A0);
  // AND_Gate and_3 has open pins: out=and_3_out
  // AND_Gate and_4 has open pins: out=and_4_out
  or or_1 (out_4, and_1_out, and_2_out, and_3_out, and_4_out);
endmodule
