// Logisim project decoder_block.circ as structural Verilog: 2 circuits, main circuit DEC
module DEC (
  input  X,
  input  Y,
  output XY,
  output X_NOTY,
  output NOTX_Y,
  output NOTX_NOTY
);

  wire not_1_out, not_2_out;

  not not_1 (not_1_out, X);
  not not_2 (not_2_out, Y);
  and and_1 (XY, X, Y);
  and and_2 (X_NOTY, X, not_2_out);
  and and_3 (NOTX_Y, not_1_out, Y);
  and and_4 (NOTX_NOTY, not_1_out, not_2_out);
endmodule

module DEC_test (
);

  Multiplexer #(.enable("false"), .select(2)) multiplexer_1 ();  // open: in0, in1, in2, in3, out, sel
  DEC dec_1 ();  // open: X, Y, XY, X_NOTY, NOTX_Y, NOTX_NOTY
endmodule
